# Fritzing sketch Ver.1 Bluetooth Head Tracking System (saved by Fritzing 0.9.3b)
breadboards: 2

parts:
  Part1 = Bluetooth HC-05 Macho
  Part3 = Arduino Uno (Rev3) - ICSP
  Part4 = InvenSense MPU6050
  M2 = Dagu DGServo 9g (Top view) [part_number=RS001B]
  Part5 = Arduino Uno (Rev3) - ICSP
  Part6 = Bluetooth HC-05 Macho
  M1 = Dagu DGServo 9g (End View) [part_number=RS001B]

nets:
  N1: Part1.TXD, Part3.D0/RX
  N2: Part1.RXD, Part3.D1/TX
  VCC: Part1.VCC, Part3.5V, Part4.VCC
  GND: Part1.GND, Part3.GND, Part4.GND
  N3: Part3.A4/SDA, Part4.SCL
  N4: Part3.A5/SCL, Part4.SDA
  GND_2: M2.gnd, Part6.GND, M1.gnd
  VCC_2: M2.vcc, Part6.VCC, M1.vcc
  N5: M2.pulse, Part5.D3_PWM
  N6: Part5.D0/RX, Part6.TXD
  N7: Part5.D1/TX, Part6.RXD
  N8: Part5.D4, M1.pulse
